// Logisim project DIGITAL LOGIC DESIGN PROJECT (TWO WAYS TRAFFIC LIGHT WITH PEDESTRIAN CROSSING SIGNAL).circ as structural Verilog
module main (
  input  in_1
);

  wire and_1_out, and_2_out, and_3_out, and_4_out, and_5_out, and_6_out, and_7_out, and_8_out, and_9_out,
       and_10_out, and_11_out, and_12_out, and_13_out, clock_1_out, j_k_ff_1_q, j_k_ff_1_qn, j_k_ff_2_q,
       j_k_ff_2_qn, j_k_ff_3_q, j_k_ff_3_qn, not_1_out, not_2_out, or_1_out, or_2_out, or_3_out, or_4_out,
       or_5_out, or_6_out;

  not not_1 (not_1_out, in_1);
  or or_1 (or_1_out, j_k_ff_3_q, j_k_ff_2_q, not_1_out);
  Clock clock_1 (.out(clock_1_out));
  and and_1 (and_1_out, j_k_ff_3_qn, j_k_ff_2_q, j_k_ff_1_qn);
  LED led_1 (.in(or_2_out));
  LED led_2 (.in(and_3_out));
  LED led_3 (.in(and_1_out));
  and and_2 (and_2_out, in_1, j_k_ff_3_q, j_k_ff_2_q);
  and and_3 (and_3_out, j_k_ff_3_q, j_k_ff_2_q, j_k_ff_1_qn);
  J_K_Flip_Flop j_k_ff_1 (
    .J(and_2_out), .clk(or_1_out), .K(clock_1_out), .Q(j_k_ff_1_q), .Qn(j_k_ff_1_qn));  // open: preset, en, reset
  and and_4 (and_4_out, j_k_ff_3_qn, j_k_ff_2_qn);
  or or_2 (or_2_out, j_k_ff_1_q, and_4_out);
  and and_5 (and_5_out, in_1, j_k_ff_3_qn);
  or or_3 (or_3_out, j_k_ff_1_q, not_1_out, j_k_ff_3_q);
  and and_6 (and_6_out, or_2_out, or_6_out);
  LED led_4 (.in(and_6_out));
  LED led_5 (.in(not_2_out));
  not not_2 (not_2_out, and_6_out);
  and and_7 (and_7_out, in_1, j_k_ff_3_q);
  or or_4 (or_4_out, and_5_out, and_7_out);
  J_K_Flip_Flop j_k_ff_2 (
    .J(or_4_out), .clk(or_3_out), .K(clock_1_out), .Q(j_k_ff_2_q), .Qn(j_k_ff_2_qn));  // open: preset, en, reset
  and and_8 (and_8_out, in_1, j_k_ff_2_qn, j_k_ff_1_q);
  and and_9 (and_9_out, j_k_ff_3_qn, j_k_ff_2_qn, j_k_ff_1_q);
  LED led_6 (.in(or_6_out));
  LED led_7 (.in(and_13_out));
  LED led_8 (.in(and_9_out));
  and and_10 (and_10_out, in_1, j_k_ff_2_q, j_k_ff_1_qn);
  and and_11 (and_11_out, not_1_out, j_k_ff_2_qn, j_k_ff_1_qn);
  or or_5 (or_5_out, and_8_out, and_10_out, and_11_out);
  J_K_Flip_Flop j_k_ff_3 (
    .J(or_5_out), .clk(j_k_ff_3_q), .K(clock_1_out), .Q(j_k_ff_3_q), .Qn(j_k_ff_3_qn));  // open: preset, en, reset
  and and_12 (and_12_out, j_k_ff_3_qn, j_k_ff_1_qn);
  or or_6 (or_6_out, j_k_ff_2_q, and_12_out);
  and and_13 (and_13_out, j_k_ff_3_q, j_k_ff_2_qn, j_k_ff_1_q);

  // Notes on the sheet:
  //     R2
  //     Y2
  //      G2
  //       PG
  //        PR
  //        R1
  //         Y1
  //       G1
endmodule
